# Fritzing sketch Untitled Sketch (saved by Fritzing 0.9.3b)
breadboards: 1

parts:
  Mod1 = Microbit
  R1 = Resistor [tolerance=±5% resistance=47 package="0805 [SMD]"]
  LED1 = smd LED [color="Red (633nm)" package="0603 [SMD]"]

nets:
  N1: Mod1.P8-bot, LED1.anode
  N2: Mod1.GND-18, Mod1.GND-41, R1.Pin_1

custom parts:
  Microbit: BBC Microbit Fritzing part. July 2020 modify to match the xxx breakout board from yyyy. Remove pcb view as unused (this is a breakout board) and add all the connectors on the breakout board (not all of which I know the purpose of at the moment.)
